// Logisim project FULL ADDER PROJECT.circ as structural Verilog: 1 circuit, main circuit main
module main (
  input  A,
  input  B,
  input  C,
  output S,
  output c_out
);

  wire AND_2_out, AND_out, XOR_out;

  xor XOR (XOR_out, A, B);
  and AND (AND_out, B, A);
  xor XOR_2 (S, XOR_out, C);
  and AND_2 (AND_2_out, C, XOR_out);
  or OR (c_out, AND_2_out, AND_out);
endmodule
