// Logisim project HALF ADDER PROJECT.circ as structural Verilog: 1 circuit, main circuit main
module main (
  input  A,
  input  B,
  output SUM_S,
  output CARRY_c
);

  and and_1 (CARRY_c, B, A);
  xor xor_1 (SUM_S, B, A);
endmodule
