// Logisim project Smart Water Tank Overflow Projection and Pump Control System.circ as structural Verilog: 1 circuit, main circuit main
module main (
  input  fulll_level_sensor__F,
  input  Medium_level_sensor__M,
  input  Low_level_sensor__L,
  input  INHIBIT_MANUAL_OFF,
  output PUMP__ON___1
);

  wire G1_OR_out, Not_L_out;

  not Not_L (Not_L_out, Low_level_sensor__L);
  or G1_OR (G1_OR_out, fulll_level_sensor__F, Medium_level_sensor__M, Not_L_out);
  and G2_AND (PUMP__ON___1, G1_OR_out, INHIBIT_MANUAL_OFF);
endmodule
